# Fritzing sketch NodeMCU-health-kiosk-schematic (saved by Fritzing 0.9.3b)
circuit board: 10.16cm x 10.16cm
breadboards: 2

parts:
  R_SDA = Resistor [tolerance=±5% resistance=4.7k package=THT]
  U3 = NodeMCU V3.0
  R1 = Resistor [tolerance=±5% resistance=220 package=THT]
  R_SCL = Resistor [tolerance=±5% resistance=4.7k package=THT]
  BP_AUTOMATION = screw terminal, 3 pins
  M5_MLX_SERIAL = screw terminal, 2 pins
  M5_TEMP_POWER = screw terminal, 2 pins
  BP_POWER = screw terminal, 2 pins
  M5_MLX_POWER = screw terminal, 2 pins
  TACTILE = screw terminal, 2 pins
  M5_TEMP_SERIAL = screw terminal, 2 pins
  J3 = male pin header, 1 pin [form="♂ (male)"]  # not connected
  J4 = male pin header, 1 pin [form="♂ (male)"]  # not connected
  J5 = male pin header, 1 pin [form="♂ (male)"]  # not connected
  J6 = male pin header, 1 pin [form="♂ (male)"]  # not connected
  J7 = male pin header, 1 pin [form="♂ (male)"]  # not connected
  J8 = male pin header, 1 pin [form="♂ (male)"]  # not connected
  J1 = male pin header, 15 pins [form="♂ (male)"]  # not connected
  J2 = male pin header, 15 pins [form="♂ (male)"]  # not connected

nets:
  N1: R_SDA.Pin_0, U3.3V3, R_SCL.Pin_0, M5_TEMP_POWER.pin2, BP_POWER.pin2, M5_MLX_POWER.pin2, TACTILE.pin2
  N2: R_SDA.Pin_1, U3.D2, M5_MLX_SERIAL.pin2, M5_TEMP_SERIAL.pin2
  N3: U3.D1, R_SCL.Pin_1, M5_MLX_SERIAL.pin1, M5_TEMP_SERIAL.pin1
  N4: U3.GND, R1.Pin_1, M5_TEMP_POWER.pin1, BP_POWER.pin1, M5_MLX_POWER.pin1
  N5: U3.D6, R1.Pin_0, TACTILE.pin1
  N6: U3.D7, BP_AUTOMATION.pin1
  N7: U3.D8, BP_AUTOMATION.pin2
  N8: U3.RX, BP_AUTOMATION.pin3

custom parts:
  NodeMCU V3.0: ESP8266 based NodeMCU (modifed for Lolin 1.1 inch module, this one with the pcb reversed and schematic fixed up).
