# Fritzing sketch RPi-health-kiosk-schematic (saved by Fritzing 0.9.3b)
circuit board: 7.62cm x 5.08cm
breadboards: 1

parts:
  C1 = Electrolytic Capacitor [capacitance=100µF package="100 mil [THT, electrolytic]"]
  J1 = Raspberry Pi Header 40pin [form="♂ (male)" package=THT]
  GSM_Main_Power = screw terminal, 2 pins
  GSM_Data = screw terminal, 3 pins
  All_Power_Button = screw terminal, 2 pins
  GPS_Module = screw terminal, 3 pins
  TS_Data = screw terminal, 2 pins
  TS_Power = screw terminal, 2 pins
  J3 = double row male pin header, 40 pins [form="♂ (male)"]  # not connected

nets:
  N1: C1.-, J1.GND, GSM_Main_Power.pin1, GSM_Data.pin1, All_Power_Button.pin1, GPS_Module.pin1, TS_Power.pin1
  N2: C1.+, J1.5V, GSM_Main_Power.pin2, TS_Power.pin2
  3V3: J1.3v3, J1.3V3, GPS_Module.pin3
  N3: J1.GPIO2, TS_Data.pin2
  N4: J1.GPIO3, TS_Data.pin1
  N5: J1.GIPO22, All_Power_Button.pin2
  N6: J1.ID_SC, GPS_Module.pin2
  N7: J1.GIPO15, GSM_Data.pin3
  N8: J1.GIPO14, GSM_Data.pin2

notes:
  GPS:
  GND - TX - VCC
  For all:
  Pin 1: GND
  GSM:
  GND - RX- TX - none - GND - VCC
  3 pin | 2 pin

custom parts:
  Raspberry Pi Header 40pin: Raspberry Pi 40 pin header - for creating your own shields.
